# Fritzing sketch Ampelschaltung (saved by Fritzing 0.9.3b)
breadboards: 1

parts:
  U1 = NodeMCU V3.0
  R2 = Resistor [tolerance=±5% resistance=220 package=THT]
  R3 = Resistor [tolerance=±5% resistance=220 package=THT]
  LED1 = LED - 5mm [color="Red (633nm)" package="5 mm [THT]"]
  LED2 = LED - 5mm [color="Yellow (585nm)" package="5 mm [THT]"]
  LED3 = LED - 5mm [color="Green (565nm)" package="5 mm [THT]"]
  R1 = Resistor [tolerance=±5% resistance=220 package=THT]
  S1 = Pushbutton [package="[THT]"]
  R4 = Resistor [tolerance=±5% resistance=1.5k package="1206 [SMD]"]

nets:
  N1: U1.D0, LED1.anode
  N2: U1.D1, LED2.anode
  N3: U1.D2, LED3.anode
  N4: U1.3V3, S1.Pin_3, S1.Pin_4
  N5: U1.D5, S1.Pin_1, S1.Pin_2, R4.Pin_1
  N6: U1.GND, R2.Pin_0, R3.Pin_0, R1.Pin_0, R4.Pin_0
  N7: R2.Pin_1, LED2.cathode
  N8: R3.Pin_1, LED3.cathode
  N9: LED1.cathode, R1.Pin_1

custom parts:
  NodeMCU V3.0: NodeMcu V3 Lua WIFI Development Board
